// Logisim project proj1.circ as structural Verilog: 1 circuit, main circuit main
module main (
  input  Ad,
  input  Bd,
  input  in_3,
  input  in_4,
  input  in_5,
  input  in_6,
  input  in_7,
  input  in_8,
  input  in_9,
  input  in_10,
  input  in_11,
  output A,
  output B,
  output O,
  output out_15,
  output _0,
  output b_2,
  output a_2,
  output ab,
  output [1:0] out_20,
  output out_21,
  output [2:0] out_22,
  output out_23
);

  wire and_2_out, and_3_out, and_4_out, and_5_out, nor_1_out, or_1_out;

  not not_1 (B, Ad);
  not not_2 (A, Bd);
  and and_1 (O, B, A);
  Decoder #(.select(2)) decoder_1 (.out0(_0), .out1(b_2), .out2(a_2), .out3(ab), .sel(out_20), .en(1'b1));
  nor nor_1 (nor_1_out, out_21, in_3);
  or or_1 (or_1_out, out_21, nor_1_out);
  Priority_Encoder priority_encoder_1 (
    .in0(in_4), .in1(in_5), .in2(in_6), .in3(in_7), .in4(in_8), .in5(in_9), .in6(in_10), .in7(in_11),
    .out(out_22), .gs(out_23));  // open: en_in, en_out
  and and_2 (and_2_out, _0, O, or_1_out);
  and and_3 (and_3_out, B, or_1_out, b_2);
  and and_4 (and_4_out, A, or_1_out, a_2);
  and and_5 (and_5_out, 1'b1, or_1_out, ab);
  assign {out_21, out_20} = ~out_22;  // NOT_Gate not_3, 3 bits wide
  or or_2 (out_15, and_2_out, and_3_out, and_4_out, and_5_out);
  Priority_Encoder priority_encoder_2 ();  // open: in0, in1, in2, in3, in4, in5, in6, in7, out, en_in, gs, en_out

  // Notes on the sheet:
  //   b
  //   a
  //   + / -
  //   0 =AB+,1=A+,2=B+,3=O+,4=AB-,5 =A-,6=B-,7=O-
endmodule
